# Fritzing sketch wiring (saved by Fritzing 0.9.3b)
breadboards: 1

parts:
  Arduino = Arduino Uno (Rev3)
  Joystick_2 = Thumb Joystick
  Joystick_1 = Thumb Joystick

nets:
  N1: Arduino.A0, Joystick_2.HORZ
  N2: Arduino.A1, Joystick_2.VERT
  N3: Arduino.A2, Joystick_1.HORZ
  N4: Arduino.A3, Joystick_1.VERT
  GND: Arduino.GND, Joystick_2.GND, Joystick_1.GND
  N5: Arduino.D2, Joystick_2.SEL
  N6: Arduino.D3_PWM, Joystick_1.SEL
  VCC: Arduino.5V, Joystick_2.VCC, Joystick_1.VCC
